# Fritzing sketch PCB-small (saved by Fritzing 0.9.2b)
circuit board: 7.62cm x 2.54cm
breadboards: 1

parts:
  U1 = Voltage Regulator [package=to220-igo]
  D1 = Diode [package=diode-1n4001]
  VIN = Battery block 9V
  Pololu_8835 = SN74LS14N [package="DIP14 [THT]"]
  Particle_Photon = Photon
  C1 = Capacitor Polarized [package=cpol-radial-100uf-25v]

nets:
  GND: U1.GND, D1.A, Pololu_8835.1A, Particle_Photon.GND, C1.-
  N1: U1.IN, D1.C
  N2: U1.OUT, Pololu_8835.1Y, Particle_Photon.VIN, C1.+
  N3: VIN.-, Pololu_8835.VCC

notes:
  PhotonBot
  8/15 Dayton, OH
  S1
  v1.0
  github.com/robtarr/photonbot
  00001
  Rob Tarr
  rob@robtarr.net
