# Fritzing sketch wiring (saved by Fritzing 0.9.2b)
breadboards: 1

parts:
  Motor_Driver = Dual VNH2SP30 Motor Driver [part_number=MD03A]
  D2 = Diode [package=diode-1n4001]
  VCC1 = Battery
  VCC2 = Battery
  VCC3 = Battery
  VCC4 = Battery
  U1 = Voltage Regulator - 5V [package="TO220 [THT]"]
  C1 = Electrolytic Capacitor [capacitance=47µF voltage=20V package="100 mil [THT, electrolytic]"]
  C2 = Ceramic Capacitor [capacitance=0.1µF package="1206 [SMD, multilayer]"]
  Particle_Photon = Photon
  Front_Center_Bumper_Switch = SWITCH-MOMENTARY-2 [package=reed_switch_plastic]
  Front_Right_Bumper_Switch = SWITCH-MOMENTARY-2 [package=reed_switch_plastic]
  Vacuum_Motor = DC Motor
  Brush_Motor = DC Motor
  Front_Left_Bumper_Switch = SWITCH-MOMENTARY-2 [package=reed_switch_plastic]
  Left_Drive_Motor = DC Motor
  Right_Drive_Motor = DC Motor
  Q1 = npn-Powertransistor [package="TO220 [THT]"]
  R1 = Resistor [tolerance=±5% resistance=10k package="0402 [SMD]"]

nets:
  N1: Motor_Driver.1INa, Particle_Photon.D5
  N2: Motor_Driver.PWM, Particle_Photon.D1
  N3: Motor_Driver.VIN, D2.C, VCC1.+, U1.input_voltage, Vacuum_Motor.pin_1, Brush_Motor.pin_1
  N4: Motor_Driver.2PWM, Particle_Photon.D0
  N5: Motor_Driver.2INb, Particle_Photon.D4
  N6: Motor_Driver.OUT_1A, Right_Drive_Motor.pin_1
  N7: Motor_Driver.OUT_1B, Right_Drive_Motor.pin_2
  N8: Motor_Driver.OUT_2A, Left_Drive_Motor.pin_1
  N9: Motor_Driver.OUT_2B, Left_Drive_Motor.pin_2
  N10: D2.A, Vacuum_Motor.pin_2, Brush_Motor.pin_2, Q1.collector
  N11: VCC1.-, VCC2.+
  N12: VCC2.-, VCC3.+
  N13: VCC3.-, VCC4.+
  GND: VCC4.-, U1.GND, C1.-, C2.0, Particle_Photon.GND, Front_Center_Bumper_Switch.1, Front_Right_Bumper_Switch.1, Front_Left_Bumper_Switch.1, Q1.emitter
  N14: U1.output_voltage, C1.+, C2.1, Particle_Photon.VIN
  N15: Particle_Photon.A0, R1.Pin_0
  N16: Particle_Photon.D2, Front_Left_Bumper_Switch.2
  N17: Particle_Photon.D3, Front_Center_Bumper_Switch.2
  N18: Particle_Photon.D6, Front_Right_Bumper_Switch.2
  N19: Q1.base, R1.Pin_1

notes:
  12V Rail
  5V Rail
