# Fritzing sketch wiring (saved by Fritzing 0.9.2b)
stripboards: 1
breadboards: 1

parts:
  Motor_Driver = Dual VNH2SP30 Motor Driver [part_number=MD03A]
  D2 = Diode [package=diode-1n4001]
  VCC1 = Battery
  VCC2 = Battery
  VCC3 = Battery
  VCC4 = Battery
  U1 = Voltage Regulator - 5V [package="TO220 [THT]"]
  C1 = Electrolytic Capacitor [capacitance=47µF voltage=20V package="100 mil [THT, electrolytic]"]
  C2 = Ceramic Capacitor [capacitance=0.1µF package="1206 [SMD, multilayer]"]
  Part2 = Photon
  Front_Center_Bumper_Switch = SWITCH-MOMENTARY-2 [package=reed_switch_plastic]
  Front_Right_Bumper_Switch = SWITCH-MOMENTARY-2 [package=reed_switch_plastic]
  Vacuum_Motor = DC Motor
  Brush_Motor = DC Motor
  Front_Left_Bumper_Switch = SWITCH-MOMENTARY-2 [package=reed_switch_plastic]
  Left_Drive_Motor = DC Motor
  Right_Drive_Motor = DC Motor

nets (from the breadboard view):
  N1: Motor_Driver.1INa, Part2.D5
  N2: Motor_Driver.PWM, Part2.D1
  N3: Motor_Driver.2PWM, Part2.D0
  N4: Motor_Driver.2INb, Part2.D4
  N5: Motor_Driver.OUT_1A, Right_Drive_Motor.pin_1
  N6: Motor_Driver.OUT_1B, Right_Drive_Motor.pin_2
  N7: Motor_Driver.OUT_2A, Left_Drive_Motor.pin_1
  N8: Motor_Driver.OUT_2B, Left_Drive_Motor.pin_2
  N9: Motor_Driver.VIN, D2.A, VCC1.+, Vacuum_Motor.pin_1, Brush_Motor.pin_1
  GND: Motor_Driver.GND, VCC4.-, U1.GND, C1.+, C2.1, Vacuum_Motor.pin_2, Brush_Motor.pin_2
  N10: D2.C, U1.input_voltage
  N11: VCC1.-, VCC2.+
  N12: VCC2.-, VCC3.+
  N13: VCC3.-, VCC4.+
  N14: U1.output_voltage, C1.-, C2.0, Part2.VIN
  N15: Part2.GND, Front_Center_Bumper_Switch.1, Front_Right_Bumper_Switch.1, Front_Left_Bumper_Switch.1
  N16: Part2.D2, Front_Left_Bumper_Switch.2
  N17: Part2.D3, Front_Center_Bumper_Switch.2
  N18: Part2.D6, Front_Right_Bumper_Switch.2
